# Fritzing sketch Scott's Project - Breadboard (saved by Fritzing 0.8.7b)
breadboards: 1

parts:
  Q1 = MOSFET-NCHANNEL [package=to220v]
  KEYPAD1 = Membrane Matrix Keypad
  L1 = Solenoid
  D1 = Rectifier Diode [part_number=1N4001 package="Melf DO-213 AB [SMD]"]
  R1 = Resistor [tolerance=±5% resistance=1 package=THT]
  LED1 = LED - 5mm [color="Red (633nm)" package="5 mm [THT]"]
  J1 = Piezo Speaker
  Netduino_2 = Netduino 2

nets:
  N1: Q1.G, Netduino_2.D11
  N2: Q1.D, Q1.S, L1.pin1, D1.anode, R1.Pin_1, J1.pin1, Netduino_2.GND
  N3: KEYPAD1.1, Netduino_2.D7
  N4: KEYPAD1.2, Netduino_2.D6
  N5: KEYPAD1.3, Netduino_2.D5
  N6: KEYPAD1.4, Netduino_2.D4
  N7: KEYPAD1.5, Netduino_2.D3
  N8: KEYPAD1.6, Netduino_2.D2
  N9: KEYPAD1.7, Netduino_2.D1
  N10: L1.pin2, D1.cathode, Netduino_2.VIN
  N11: R1.Pin_0, LED1.anode
  N12: LED1.cathode, Netduino_2.D13
  N13: J1.pin2, Netduino_2.D10

notes:
  12v Power
  Matrix Keypad
  Speaker
  LED
  Solenoid
  MOSFET

custom parts:
  Membrane Matrix Keypad: Membrane Matrix 3x4 Keypad
  Netduino 2: An open-source electronics platform using the .NET Micro Framework
